// Logisim project timer_.circ as structural Verilog: 2 circuits, main circuit main
module main (
  input  [3:0] boutons,
  input  [2:0] etat,
  input  [22:0] temps,
  output sous_systeme,
  output [22:0] temps_restant,
  output sonne
);

  wire actif_q, and_1_out, and_2_out, and_3_out, and_4_out, and_5_out, and_6_out, and_7_out, and_8_out,
       and_9_out, comparator_1_eq, comparator_2_eq, comparator_3_gt, comparator_4_gt, comparator_5_gt,
       d_ff_2_q, d_ff_3_q, d_ff_4_q, nor_1_out, or_1_out, subtractor_1_bout, undriven, undriven_2, undriven_3;
  wire [5:0] adder_5_out, adder_6_out, adder_7_out, multiplexer_6_out, multiplexer_7_out, multiplexer_8_out,
       register_2_q, register_3_q, register_4_q;
  wire [22:0] adder_1_out, adder_2_out, adder_3_out, adder_4_out, duree_q, fin_q, multiplexer_1_out,
       multiplexer_2_out, multiplexer_3_out, multiplexer_4_out, register_1_q, subtractor_1_out,
       subtractor_2_out;

  Comparator #(.width(3), .mode("unsigned")) comparator_1 (.a(etat), .b(3'b011), .eq(comparator_1_eq));  // open: gt, lt
  D_Flip_Flop d_ff_1 (.D(1'b1), .clk(and_1_out), .Q(sous_systeme), .reset(d_ff_4_q));  // open: Qn, preset
  and and_1 (and_1_out, boutons[1], ~actif_q, comparator_1_eq);  // AND_Gate
  and and_2 (and_2_out, boutons[2], ~sous_systeme, comparator_1_eq);  // AND_Gate
  or or_1 (or_1_out, and_2_out, 1'b0);
  T_Flip_Flop actif (.T(comparator_1_eq), .clk(or_1_out), .Q(actif_q));  // open: Qn, reset, preset
  and and_3 (and_3_out, sous_systeme, ~d_ff_2_q);  // AND_Gate
  D_Flip_Flop d_ff_2 (.D(sous_systeme), .clk(boutons[2]), .Q(d_ff_2_q), .reset(d_ff_4_q));  // open: Qn, preset
  Register #(.width(23)) duree (.D(register_1_q), .clk(comparator_1_eq), .Q(duree_q));  // open: en, clr
  and and_4 (and_4_out, boutons[2], actif_q);
  and and_5 (and_5_out, d_ff_2_q, ~d_ff_3_q);  // AND_Gate
  D_Flip_Flop d_ff_3 (.D(d_ff_2_q), .clk(boutons[2]), .Q(d_ff_3_q), .reset(d_ff_4_q));  // open: Qn, preset
  Register #(.width(23)) debut (.D(temps), .clk(and_4_out));  // open: en, Q, clr
  and and_6 (and_6_out, d_ff_3_q, ~d_ff_4_q);  // AND_Gate
  D_Flip_Flop d_ff_4 (.D(d_ff_3_q), .clk(boutons[2]), .Q(d_ff_4_q), .reset(d_ff_4_q));  // open: Qn, preset
  Adder #(.width(23)) adder_1 (.a(duree_q), .b(temps), .out(adder_1_out));  // open: cin, cout
  Subtractor #(.width(23)) subtractor_1 (
    .a(adder_1_out), .b(23'h5c4900), .out(subtractor_1_out), .bout(subtractor_1_bout));  // open: bin
  Register #(.width(23)) fin (.D(multiplexer_1_out), .clk(and_4_out), .Q(fin_q));  // open: en, clr
  Multiplexer #(.width(23), .enable("false")) multiplexer_1 (
    .in0(subtractor_1_out), .in1(adder_1_out), .out(multiplexer_1_out), .sel(subtractor_1_bout));
  and and_7 (and_7_out, and_3_out, boutons[0]);
  and and_8 (and_8_out, and_5_out, boutons[0]);
  and and_9 (and_9_out, and_6_out, boutons[0]);
  Comparator #(.width(23), .mode("unsigned")) comparator_2 (
    .a(fin_q), .b(temps), .eq(comparator_2_eq));  // open: gt, lt
  and and_10 (sonne, comparator_2_eq, actif_q);
  Adder #(.width(23)) adder_2 (.a(register_1_q), .b(23'h8ca0), .out(adder_2_out));  // open: cin, cout
  Adder #(.width(23)) adder_3 (.a(multiplexer_2_out), .b(23'h258), .out(adder_3_out));  // open: cin, cout
  Adder #(.width(23)) adder_4 (.a(multiplexer_3_out), .b(23'ha), .out(adder_4_out));  // open: cin, cout
  Subtractor #(.width(23)) subtractor_2 (.a(fin_q), .b(temps), .out(subtractor_2_out));  // open: bin, bout
  Multiplexer #(.width(23), .enable("false")) multiplexer_2 (
    .in0(register_1_q), .in1(adder_2_out), .out(multiplexer_2_out), .sel(and_7_out));
  Multiplexer #(.width(23), .enable("false")) multiplexer_3 (
    .in0(multiplexer_2_out), .in1(adder_3_out), .out(multiplexer_3_out), .sel(and_8_out));
  Multiplexer #(.width(23), .enable("false")) multiplexer_4 (
    .in0(multiplexer_3_out), .in1(adder_4_out), .out(multiplexer_4_out), .sel(and_9_out));
  Multiplexer #(.width(23), .enable("false")) multiplexer_5 (
    .in0(duree_q), .in1(subtractor_2_out), .out(temps_restant), .sel(actif_q));
  Register #(.width(23)) register_1 (.D(multiplexer_4_out), .clk(nor_1_out), .Q(register_1_q));  // open: en, clr
  nor nor_1 (nor_1_out, and_7_out, and_8_out, and_9_out);
  Register #(.width(6)) register_2 (.D(adder_5_out), .clk(undriven_3), .Q(register_2_q));  // open: en, clr
  Adder #(.width(6)) adder_5 (.a(multiplexer_6_out), .b(6'b000001), .out(adder_5_out));  // open: cin, cout
  Register #(.width(6)) register_3 (.D(adder_6_out), .clk(undriven), .Q(register_3_q));  // open: en, clr
  Adder #(.width(6)) adder_6 (.a(multiplexer_7_out), .b(6'b000001), .out(adder_6_out));  // open: cin, cout
  Register #(.width(6)) register_4 (.D(adder_7_out), .clk(undriven_2), .Q(register_4_q));  // open: en, clr
  Adder #(.width(6)) adder_7 (.a(multiplexer_8_out), .b(6'b000001), .out(adder_7_out));  // open: cin, cout
  Comparator #(.width(6), .mode("unsigned")) comparator_3 (
    .a(register_2_q), .b(6'b010111), .gt(comparator_3_gt));  // open: eq, lt
  Comparator #(.width(6), .mode("unsigned")) comparator_4 (
    .a(register_3_q), .b(6'b000101), .gt(comparator_4_gt));  // open: eq, lt
  Comparator #(.width(6), .mode("unsigned")) comparator_5 (
    .a(register_4_q), .b(6'b001001), .gt(comparator_5_gt));  // open: eq, lt
  Multiplexer #(.width(6), .enable("false")) multiplexer_6 (
    .in0(register_2_q), .in1({6{1'b0}}), .out(multiplexer_6_out), .sel(comparator_3_gt));
  Multiplexer #(.width(6), .enable("false")) multiplexer_7 (
    .in0(register_3_q), .in1({6{1'b0}}), .out(multiplexer_7_out), .sel(comparator_4_gt));
  Multiplexer #(.width(6), .enable("false")) multiplexer_8 (
    .in0(register_4_q), .in1({6{1'b0}}), .out(multiplexer_8_out), .sel(comparator_5_gt));

  // Notes on the sheet:
  //   De plus, si je veux que ça démarre tout de suite après le set, faire que debut et fin soient set aussi
  //   A faire : gerer que le temps set soit mis dans durée. 
  //   en fait, il faut trigger le bouton start
  //   incrémenter valeur du mode set 
  //   passer au segment suivant du set
  //   mode set
  //   reset (inutile ?)
  //   ne pas mettre de sortie, mais changer l'état à SONNE (100)
endmodule

module Timer (
  input  [3:0] Boutons,
  input  [2:0] Etat,
  input  [22:0] Temps
);

  wire comparator_1_eq;

  Comparator #(.width(3)) comparator_1 (.a(Etat), .b(3'b011), .eq(comparator_1_eq));  // open: gt, lt
endmodule
